// Logisim project CPU_1114_01_03.circ as structural Verilog
module main (
  input  A,
  input  B,
  input  A_2,
  input  B_2,
  input  A_3,
  input  A_4,
  input  B_3,
  input  A_5,
  input  B_4,
  output NAND_OUT,
  output AND_OUT,
  output NOT_OUT,
  output OR_OUT,
  output XOR_OUT
);

  wire nand_1_out, nand_2_out, nand_3_out, nand_4_out, nand_5_out, nand_6_out;

  nand nand_1 (nand_1_out, A_5, B_4);
  nand nand_2 (nand_2_out, A_2, B_2);
  nand nand_3 (nand_3_out, A_4, A_4);
  nand nand_4 (nand_4_out, B_3, B_3);
  nand nand_5 (nand_5_out, A_5, nand_1_out);
  nand nand_6 (nand_6_out, nand_1_out, B_4);
  nand nand_7 (NAND_OUT, A, B);
  nand nand_8 (AND_OUT, nand_2_out, nand_2_out);
  nand nand_9 (NOT_OUT, A_3, A_3);
  nand nand_10 (OR_OUT, nand_3_out, nand_4_out);
  nand nand_11 (XOR_OUT, nand_5_out, nand_6_out);
endmodule

module M1 (
  input  I,
  input  S,
  output O
);

  wire nand_1_out, nand_2_out, nand_4_out;

  nand nand_1 (nand_1_out, I, S);
  nand nand_2 (nand_2_out, nand_1_out, S);
  nand nand_3 (O, nand_1_out, nand_4_out);
  nand nand_4 (nand_4_out, O, nand_2_out);
endmodule

module M8 (
  input  [7:0] I,
  input  S,
  output [7:0] O
);

  M1 m1_1 (.I(I[0]), .S(S), .O(O[0]));
  M1 m1_2 (.I(I[1]), .S(S), .O(O[1]));
  M1 m1_3 (.I(I[2]), .S(S), .O(O[2]));
  M1 m1_4 (.I(I[3]), .S(S), .O(O[3]));
  M1 m1_5 (.I(I[4]), .S(S), .O(O[4]));
  M1 m1_6 (.I(I[5]), .S(S), .O(O[5]));
  M1 m1_7 (.I(I[6]), .S(S), .O(O[6]));
  M1 m1_8 (.I(I[7]), .S(S), .O(O[7]));
endmodule

module Enabler_old (
  input  [7:0] I,
  input  S,
  output [7:0] O
);

  and and_1 (O[0], I[0], S);
  and and_2 (O[1], I[1], S);
  and and_3 (O[2], I[2], S);
  and and_4 (O[3], I[3], S);
  and and_5 (O[4], I[4], S);
  and and_6 (O[5], I[5], S);
  and and_7 (O[6], I[6], S);
  and and_8 (O[7], I[7], S);
endmodule

module Enabler (
  input  [7:0] I,
  input  EN,
  output [7:0] O
);

  assign O = EN ? I : 8'bz;  // Controlled_Buffer controlled_buffer_1
endmodule

module M8_Register (
  input  [7:0] I,
  input  S,
  input  EN,
  output [7:0] O
);

  wire [7:0] m8_1_o;

  M8 m8_1 (.I(I), .S(S), .O(m8_1_o));
  Enabler enabler_1 (.I(m8_1_o), .EN(EN), .O(O));
endmodule

module _03_bus_test (
  input  [7:0] in_1,
  input  S,
  input  S_2,
  input  EN,
  input  EN_2,
  output [7:0] out_6,
  output [7:0] out_7,
  output [7:0] out_8
);

  wire nor_1_out;

  nor nor_1 (nor_1_out, EN_2, EN);
  assign out_6 = nor_1_out ? in_1 : 8'bz;  // Controlled_Buffer controlled_buffer_1
  assign out_6 = EN ? out_7 : 8'bz;  // Controlled_Buffer controlled_buffer_2
  M8_Register RA (.I(out_6), .S(S), .EN(EN), .O(out_7));
  assign out_6 = EN_2 ? out_8 : 8'bz;  // Controlled_Buffer controlled_buffer_3
  M8_Register RA_2 (.I(out_6), .S(S_2), .EN(EN_2), .O(out_8));
endmodule

module _04_decoder (
  input  [2:0] SEL,
  output OUT_0,
  output OUT_1,
  output OUT_2,
  output OUT_3,
  output OUT_4,
  output OUT_5,
  output OUT_6,
  output OUT_7
);

  Decoder #(.enable("false"), .select(3)) decoder_1 (
    .out0(OUT_0), .out1(OUT_1), .out2(OUT_2), .out3(OUT_3), .out4(OUT_4), .out5(OUT_5), .out6(OUT_6),
    .out7(OUT_7), .sel(SEL));
endmodule

module decoder_basic (
  input  S2,
  input  S1,
  input  S0,
  output OUT_0,
  output OUT_1,
  output OUT_2,
  output OUT_3,
  output OUT_4,
  output OUT_5,
  output OUT_6,
  output OUT_7
);

  wire not_1_out, not_2_out, not_3_out;

  not not_1 (not_1_out, S2);
  not not_2 (not_2_out, S1);
  not not_3 (not_3_out, S0);
  and and_1 (OUT_0, not_1_out, not_2_out, not_3_out);
  and and_2 (OUT_1, not_1_out, not_2_out, not_3_out);
  and and_3 (OUT_2, not_1_out, S1, not_3_out);
  and and_4 (OUT_3, not_1_out, S1, S0);
  and and_5 (OUT_4, S2, not_2_out, not_3_out);
  and and_6 (OUT_5, S2, not_2_out, not_3_out);
  and and_7 (OUT_6, S2, not_2_out, S0);
  and and_8 (OUT_7, S2, S1, S0);
endmodule

module RAM256 (
);

  RAM ram_1 ();  // open: addr, data, sel, clk, ld, clr
endmodule
