// Logisim project CPU_1114_06_12.circ as structural Verilog
module main (
  input  A,
  input  B,
  input  A_2,
  input  B_2,
  input  A_3,
  input  A_4,
  input  B_3,
  input  A_5,
  input  B_4,
  output NAND_OUT,
  output AND_OUT,
  output NOT_OUT,
  output OR_OUT,
  output XOR_OUT
);

  wire nand_1_out, nand_2_out, nand_3_out, nand_4_out, nand_5_out, nand_6_out;

  nand nand_1 (nand_1_out, A_5, B_4);
  nand nand_2 (nand_2_out, A_2, B_2);
  nand nand_3 (nand_3_out, A_4, A_4);
  nand nand_4 (nand_4_out, B_3, B_3);
  nand nand_5 (nand_5_out, A_5, nand_1_out);
  nand nand_6 (nand_6_out, nand_1_out, B_4);
  nand nand_7 (NAND_OUT, A, B);
  nand nand_8 (AND_OUT, nand_2_out, nand_2_out);
  nand nand_9 (NOT_OUT, A_3, A_3);
  nand nand_10 (OR_OUT, nand_3_out, nand_4_out);
  nand nand_11 (XOR_OUT, nand_5_out, nand_6_out);
endmodule

module M1 (
  input  I,
  input  S,
  output O
);

  wire nand_1_out, nand_2_out, nand_4_out;

  nand nand_1 (nand_1_out, I, S);
  nand nand_2 (nand_2_out, nand_1_out, S);
  nand nand_3 (O, nand_1_out, nand_4_out);
  nand nand_4 (nand_4_out, O, nand_2_out);
endmodule

module M8 (
  input  [7:0] I,
  input  S,
  output [7:0] O
);

  M1 m1_1 (.I(I[0]), .S(S), .O(O[0]));
  M1 m1_2 (.I(I[1]), .S(S), .O(O[1]));
  M1 m1_3 (.I(I[2]), .S(S), .O(O[2]));
  M1 m1_4 (.I(I[3]), .S(S), .O(O[3]));
  M1 m1_5 (.I(I[4]), .S(S), .O(O[4]));
  M1 m1_6 (.I(I[5]), .S(S), .O(O[5]));
  M1 m1_7 (.I(I[6]), .S(S), .O(O[6]));
  M1 m1_8 (.I(I[7]), .S(S), .O(O[7]));
endmodule

module Enabler_old (
  input  [7:0] I,
  input  S,
  output [7:0] O
);

  and and_1 (O[0], I[0], S);
  and and_2 (O[1], I[1], S);
  and and_3 (O[2], I[2], S);
  and and_4 (O[3], I[3], S);
  and and_5 (O[4], I[4], S);
  and and_6 (O[5], I[5], S);
  and and_7 (O[6], I[6], S);
  and and_8 (O[7], I[7], S);
endmodule

module Enabler (
  input  [7:0] I,
  input  EN,
  output [7:0] O
);

  assign O = EN ? I : 8'bz;  // Controlled_Buffer controlled_buffer_1
endmodule

module M8_Register (
  input  [7:0] I,
  input  S,
  input  EN,
  output [7:0] O
);

  wire [7:0] m8_1_o;

  M8 m8_1 (.I(I), .S(S), .O(m8_1_o));
  Enabler enabler_1 (.I(m8_1_o), .EN(EN), .O(O));
endmodule

module _03_bus_test (
  input  [7:0] in_1,
  input  S,
  input  S_2,
  input  EN,
  input  EN_2,
  output [7:0] out_6,
  output [7:0] out_7,
  output [7:0] out_8
);

  wire nor_1_out;

  nor nor_1 (nor_1_out, EN_2, EN);
  assign out_6 = nor_1_out ? in_1 : 8'bz;  // Controlled_Buffer controlled_buffer_1
  assign out_6 = EN ? out_7 : 8'bz;  // Controlled_Buffer controlled_buffer_2
  M8_Register RA (.I(out_6), .S(S), .EN(EN), .O(out_7));
  assign out_6 = EN_2 ? out_8 : 8'bz;  // Controlled_Buffer controlled_buffer_3
  M8_Register RA_2 (.I(out_6), .S(S_2), .EN(EN_2), .O(out_8));
endmodule

module _04_decoder (
  input  [2:0] SEL,
  output OUT_0,
  output OUT_1,
  output OUT_2,
  output OUT_3,
  output OUT_4,
  output OUT_5,
  output OUT_6,
  output OUT_7
);

  Decoder #(.enable("false"), .select(3)) decoder_1 (
    .out0(OUT_0), .out1(OUT_1), .out2(OUT_2), .out3(OUT_3), .out4(OUT_4), .out5(OUT_5), .out6(OUT_6),
    .out7(OUT_7), .sel(SEL));
endmodule

module decoder_basic (
  input  S2,
  input  S1,
  input  S0,
  output OUT_0,
  output OUT_1,
  output OUT_2,
  output OUT_3,
  output OUT_4,
  output OUT_5,
  output OUT_6,
  output OUT_7
);

  wire not_1_out, not_2_out, not_3_out;

  not not_1 (not_1_out, S2);
  not not_2 (not_2_out, S1);
  not not_3 (not_3_out, S0);
  and and_1 (OUT_0, not_1_out, not_2_out, not_3_out);
  and and_2 (OUT_1, not_1_out, not_2_out, not_3_out);
  and and_3 (OUT_2, not_1_out, S1, not_3_out);
  and and_4 (OUT_3, not_1_out, S1, S0);
  and and_5 (OUT_4, S2, not_2_out, not_3_out);
  and and_6 (OUT_5, S2, not_2_out, not_3_out);
  and and_7 (OUT_6, S2, not_2_out, S0);
  and and_8 (OUT_7, S2, S1, S0);
endmodule

module _05_RAMv1 (
  input  x,
  input  y,
  input  b_s,
  input  b_e,
  input  [7:0] b_i,
  output [7:0] b_o
);

  wire and_1_out, and_2_out, and_3_out;
  wire [7:0] controlled_buffer_1_out, m8_register_1_o;

  and and_1 (and_1_out, y, x);
  and and_2 (and_2_out, and_1_out, b_s);
  and and_3 (and_3_out, and_1_out, b_e);
  assign controlled_buffer_1_out = and_1_out ? b_i : 8'bz;  // Controlled_Buffer controlled_buffer_1
  assign b_o = and_1_out ? m8_register_1_o : 8'bz;  // Controlled_Buffer controlled_buffer_2
  M8_Register m8_register_1 (.I(controlled_buffer_1_out), .S(and_2_out), .EN(and_3_out), .O(m8_register_1_o));
endmodule

module RAM256 (
  input  [7:0] addr,
  input  s,
  input  [7:0] in_val,
  output [7:0] out_val
);

  wire clik_out;

  Button clik (.out(clik_out));
  RAM ram_1 (.addr(addr), .we(s), .oe(clik_out), .din(in_val), .dout(out_val));  // open: clk
endmodule

module _06_Adder (
  input  Ci,
  input  [7:0] A,
  input  [7:0] B,
  output [7:0] S,
  output Co
);

  Adder adder_1 (.a(A), .b(B), .out(S), .cin(Ci), .cout(Co));
endmodule

module HA (
  input  A,
  input  B,
  output S,
  output Co
);

  xor xor_1 (S, A, B);
  and and_1 (Co, A, B);
endmodule

module FA (
  input  A,
  input  B,
  input  Ci,
  output S,
  output Co
);

  wire ha_1_co, ha_1_s, ha_2_co;

  HA ha_1 (.A(A), .B(B), .S(ha_1_s), .Co(ha_1_co));
  HA ha_2 (.A(ha_1_s), .B(Ci), .S(S), .Co(ha_2_co));
  or or_1 (Co, ha_2_co, ha_1_co);
endmodule

module _07_Shift (
  input  [7:0] in_1,
  input  in_2,
  input  [7:0] in_3,
  input  in_4,
  output out_5,
  output [7:0] out_6,
  output out_7,
  output [7:0] out_8
);

  SHR shr_1 (.i(in_1), .si(in_2), .so(out_5), .o(out_6));
  SHL shl_1 (.i(in_3), .si(in_4), .so(out_7), .o(out_8));
endmodule

module SHR (
  input  [7:0] i,
  input  si,
  output so,
  output [7:0] o
);

  wire [7:1] m8_register_1_o;

  M8_Register m8_register_1 (.I(i), .S(1'b1), .EN(1'b1), .O({m8_register_1_o, so}));
  M8_Register m8_register_2 (.I({si, m8_register_1_o}), .S(1'b1), .EN(1'b1), .O(o));
endmodule

module SHL (
  input  [7:0] i,
  input  si,
  output so,
  output [7:0] o
);

  wire [6:0] m8_register_1_o;

  M8_Register m8_register_1 (.I(i), .S(1'b1), .EN(1'b1), .O({si, m8_register_1_o}));
  M8_Register m8_register_2 (.I({m8_register_1_o, so}), .S(1'b1), .EN(1'b1), .O(o));
endmodule

module inveter (
  input  [7:0] i,
  output [7:0] o
);

  assign o = ~i;  // NOT_Gate not_1, 8 bits wide
endmodule

module ANDer (
  input  [7:0] a,
  input  [7:0] b,
  output [7:0] o
);

  assign o = a & b;  // AND_Gate and_1, 8 bits wide
endmodule

module ORer (
  input  [7:0] a,
  input  [7:0] b,
  output [7:0] o
);

  assign o = a | b;  // OR_Gate or_1, 8 bits wide
endmodule

module XORer (
  input  [7:0] a,
  input  [7:0] b,
  output [7:0] o
);

  assign o = a ^ b;  // XOR_Gate xor_1, 8 bits wide
endmodule

module ZEROer (
  input  [7:0] in,
  output out_2
);

  wire or_1_out;

  or or_1 (or_1_out, in[0], in[1], in[2], in[3], in[4], in[5], in[6], in[7]);
  not not_1 (out_2, or_1_out);
endmodule
